# Fritzing sketch IC Sketch (saved by Fritzing 0.9.9b)
breadboards: 1

parts:
  Componente2 = Arduino Uno (Rev3)
  SM1 = 28BYJ-48 Stepper Motor [part_number=28BYJ-48]
  Driver1 = 28BYJ-48 Driver Module [part_number=ULN2003 package=THT]
  SM2 = 28BYJ-48 Stepper Motor [part_number=28BYJ-48]
  Driver2 = 28BYJ-48 Driver Module [part_number=ULN2003 package=THT]

nets:
  N1: Componente2.D8, Driver2.IN4
  N2: Componente2.D9_PWM, Driver2.IN3
  N3: Componente2.D10_PWM/SS, Driver2.IN2
  N4: Componente2.D11_PWM/MOSI, Driver2.IN1
  N5: Componente2.D4, Driver1.IN1
  N6: Componente2.D5_PWM, Driver1.IN2
  N7: Componente2.D6_PWM, Driver1.IN3
  N8: Componente2.D7, Driver1.IN4
  N9: Componente2.5V, Driver1.Vmotor, Driver2.Vmotor
  GND: Componente2.GND, Driver1.GND, Driver2.GND
  N10: SM1.blue-pin, Driver1.blue-pin
  N11: SM1.pink-pin, Driver1.pink-pin
  N12: SM1.yellow-pin, Driver1.yellow-pin
  N13: SM1.orange-pin, Driver1.orange-pin
  N14: SM1.red-pin, Driver1.red-pin
  N15: SM2.blue-pin, Driver2.blue-pin
  N16: SM2.pink-pin, Driver2.pink-pin
  N17: SM2.yellow-pin, Driver2.yellow-pin
  N18: SM2.orange-pin, Driver2.orange-pin
  N19: SM2.red-pin, Driver2.red-pin

custom parts:
  28BYJ-48 Stepper Motor: Unipolar Stepper Motor 28BYJ-48 Top coil - pink & orange Bottom coil - blue & yellow Common rail - red Connector pins: blue - pink - yellow - orange - red
  28BYJ-48 Driver Module: ULN2003 Driver Module for the 28BYJ-48 Unipolar Stepper Motor LED A - Blue wire - Bottom coil left LED B - Pink wire - Top coil left LED C - Yellow wire - Bottom coil right LED D - Orange wire - Top coil right Common rail - red Connector pins: blue - pink - yellow - orange - red Control pins - IN1 to IN4 Power pins - GND & Vmotor (5-12V) On/Off jumper (if removed, power to motor is cut).
